# Fritzing sketch LocalHub (saved by Fritzing 0.9.3b)

parts:
  Часть1 = BluePill
  Часть2 = NRF24L01+ Breakout Board
  C1 = Electrolytic Capacitor [capacitance=1µF package="100 mil [THT, electrolytic]"]
  U1 = 74HC595 [package="DIP16 [THT]"]
  U2 = 74HC595 [package="DIP16 [THT]"]
  LED2 = LED - 5mm [color="Yellow (595nm)" package="5 mm [THT]"]
  LED3 = LED - 5mm [color="Green (565nm)" package="5 mm [THT]"]
  R1 = Resistor [tolerance=±5% resistance=220 package=THT]  # not connected
  LED4 = LED - 5mm [color="Red (660nm)" package="5 mm [THT]"]
  R2 = Resistor [tolerance=±5% resistance=220 package=THT]  # not connected
  R3 = Resistor [tolerance=±5% resistance=220 package=THT]
  S1 = Pushbutton [package="[SMD]"]
  S2 = Pushbutton [package="[SMD]"]
  S3 = Pushbutton [package="[SMD]"]

nets:
  N1: Часть1.C13, LED3.anode
  N2: Часть1.C14, LED2.anode
  N3: Часть1.C15, LED4.anode
  N4: Часть1.A3, Часть2.CS
  N5: Часть1.A4, Часть2.CE
  N6: Часть1.A5, Часть1.B0, Часть1.GND2, Часть1.B1, S1.Pin_3, S1.Pin_4, S2.Pin_3, S2.Pin_4, S3.Pin_3, S3.Pin_4
  N7: Часть1.A6, Часть2.MISO
  N8: Часть1.A7, Часть2.MOSI
  3V3: Часть1.3V3, Часть2.VCC, C1.+
  GND: Часть1.GND, Часть2.GND
  N9: Часть1.GND3, U1.OE, U2.OE, R3.Pin_1
  VCC: Часть1.5V, U1.VCC, U2.VCC
  N10: Часть1.B15, U1.DS
  N11: Часть1.B13, U1.SH_CP, U2.SH_CP
  N12: Часть1.B12, U1.ST_CP, U2.ST_CP
  N13: Часть1.A2, Часть2.IRQ
  N14: Часть2.SCK, C1.-
  GND_2: U1.GND, U2.GND
  N15: U1.Q7', U2.DS

notes:
  PortA
  portB
  portC
  i2c
  CAN
  UART
  SPI
